# Fritzing sketch CapacitiveCover (saved by Fritzing 0.7.12b)
breadboards: 1

parts:
  Arduino1 = Arduino
  R1 = Resistor [tolerance=±5% resistance=20M package=THT]
  R2 = 220 Ω Resistor [package=THT]  # not connected

nets:
  N1: Arduino1.D4, R1.Pin_1
  N2: Arduino1.D2, R1.Pin_0

custom parts:
  220 Ω Resistor: A generic resistor (0.25W)
