# Fritzing sketch FeedbackLoop (saved by Fritzing 0.7.12b)
breadboards: 1

parts:
  Arduino1 = Arduino
  LED1 = LED - 5mm [color="Red (633nm)" package="5 mm [THT]"]
  R1 = Resistor [tolerance=±5% resistance=220 package=THT]
  S1 = Pushbutton [package="[THT]"]

nets:
  N1: Arduino1.D13, LED1.anode
  N2: Arduino1.D2, R1.Pin_0, S1.Pin_1, S1.Pin_2
  N3: Arduino1.+5V, S1.Pin_3, S1.Pin_4
  N4: Arduino1.GND, LED1.cathode, R1.Pin_1
