# Fritzing sketch RGB-LED (saved by Fritzing 0.8.4b)
breadboards: 1

parts:
  R5 = Resistor [tolerance=±5% resistance=220 package=THT]
  R6 = Resistor [tolerance=±5% resistance=220 package=THT]
  R4 = Resistor [tolerance=±5% resistance=220 package=THT]
  LED1 = RGB LED - (4 legs) [package="5 mm [THT]"]
  R3 = Rotary Potentiometer (Small) [maximum_resistance=100kΩ package=THT]
  R2 = Rotary Potentiometer (Small) [maximum_resistance=100kΩ package=THT]
  R1 = Rotary Potentiometer (Small) [maximum_resistance=100kΩ package=THT]
  Arduino1 = Arduino Uno (Rev3)

nets:
  N1: R5.Pin_0, Arduino1.D11_PWM/MOSI
  N2: R5.Pin_1, LED1.green_cathode
  N3: R6.Pin_0, Arduino1.D9_PWM
  N4: R6.Pin_1, LED1.red_cathode
  N5: R4.Pin_0, Arduino1.D10_PWM/SS
  N6: R4.Pin_1, LED1.blue_cathode
  N7: LED1.common_anode, R3.leg2, R2.leg2, R1.leg2, Arduino1.GND
  N8: R3.leg1, R2.leg1, R1.leg1, Arduino1.5V
  N9: R3.wiper, Arduino1.A5/SCL
  N10: R2.wiper, Arduino1.A3
  N11: R1.wiper, Arduino1.A1
