# Fritzing sketch TemperatureSensor (saved by Fritzing 0.7.12b)

parts:
  Arduino1 = Arduino
  R1 = Resistor [tolerance=±5% resistance=220 package=THT]
  R2 = Resistor [tolerance=±5% resistance=220 package=THT]
  R3 = Resistor [tolerance=±5% resistance=220 package=THT]
  LED1 = RGB LED (com. cathode, rbg) [package="5 mm [THT]"]
  T1 = LM35 Temperature Sensor [package="TO92 [THT]"]

nets:
  N1: Arduino1.D11, R2.Pin_0
  N2: Arduino1.D10, R1.Pin_0
  N3: Arduino1.D9, R3.Pin_1
  N4: Arduino1.3V3, T1.+Vs
  N5: Arduino1.+5V, LED1.common_cathode
  GND: Arduino1.GND, T1.GND
  N6: Arduino1.A2, T1.Vout
  N7: R1.Pin_1, LED1.green_anode
  N8: R2.Pin_1, LED1.blue_anode
  N9: R3.Pin_0, LED1.red_anode
