# Fritzing sketch Servomotor (saved by Fritzing 0.7.10b)
breadboards: 1

parts:
  Arduino1 = Arduino
  J2 = Basic Servo
  J3 = Basic Servo

nets:
  GND: Arduino1.GND, J2.gnd, J3.gnd
  N1: Arduino1.D10, J2.pulse
  N2: Arduino1.D9, J3.pulse
  VCC: Arduino1.+5V, J2.vcc, J3.vcc
